# Fritzing sketch erni 14 vie (saved by Fritzing 1.0.5)

parts:
  A1 = Raspberry Pi 5
  U1 = Sharp PC817 [package=THT]
  Verde = Pushbutton [package="[SMD]"]
  24v = Battery Holders [package=battcon_245mm]
  U2 = Sharp PC817 [package=THT]
  Top/Bottom_(I1_1) = Pushbutton [package="[SMD]"]
  Galben = Pushbutton [package="[SMD]"]
  U3 = Sharp PC817 [package=THT]
  A2 = Waveshare e-Paper HAT with 7in display [package=THT]  # not connected
  U4 = MMDT3904 [package=sot363]

nets:
  N1: A1.GPIO2, U4.G$2_B
  N2: A1.5V, A1.Fan-5V, U4.G$1_E
  N3: A1.GPIO3, U4.G$1_B
  N4: A1.GND, A1.Fan-GND, U1.Pin_3, U2.Pin_3, U4.G$1_C
  N5: A1.GPIO17, U1.Pin_4
  N6: A1.GPIO27, U2.Pin_4
  N7: A1.GPIO26, U3.Pin_4
  N8: U1.Pin_1, Verde.Pin_3, Verde.Pin_4
  N9: U1.Pin_2, 24v.+, U2.Pin_2
  N10: 24v.-, U2.Pin_1, Top/Bottom_(I1_1).Pin_3, Top/Bottom_(I1_1).Pin_4
  N11: Galben.Pin_3, Galben.Pin_4, U3.Pin_1

custom parts:
  Raspberry Pi 5: The RPi5, a faster version of the awesome Raspberry Pi4B ARM Board with 40 pin gpio.
  Waveshare e-Paper HAT with 7in display: .This is a universal driver board for e-Paper raw panels, can be used to drive various SPI interface e-Paper from Waveshare. This version includes a 7in display panel in breadboard.
